// Logisim project lab2-d1.circ as structural Verilog: 1 circuit, main circuit main
module main (
  input  in_1,
  input  in_2,
  input  in_3,
  input  in_4,
  input  in_5,
  input  in_6,
  input  in_7,
  input  in_8,
  input  in_9,
  input  in_10,
  input  in_11,
  input  in_12,
  output out_13,
  output out_14,
  output out_15,
  output out_16,
  output out_17,
  output out_18
);

  wire nand_1_out, nand_2_out, NAND_3_out;

  nand nand_1 (nand_1_out, in_9, in_10);
  nand nand_2 (nand_2_out, in_11, in_12);
  and AND (out_13, in_1, in_2);
  nand NAND_3 (NAND_3_out, in_3, in_4);
  not not_1 (out_15, in_5);
  nand NAND_4 (out_16, in_6, in_6);
  or or_1 (out_17, in_7, in_8);
  nand NAND_5 (out_14, NAND_3_out, NAND_3_out);
  nand nand_6 (out_18, nand_1_out, nand_2_out);

  // Notes on the sheet:
  //   NOT
endmodule
