// Logisim project lab2-d2.2.circ as structural Verilog: 1 circuit, main circuit main
module main (
  input  A,
  input  B,
  input  A_2,
  input  B_2,
  output AB____A_B__prime,
  output out_6
);

  wire nor_1_out, nor_2_out, nor_3_out, nor_4_out, nor_5_out, nor_6_out, nor_7_out;

  nor nor_1 (nor_1_out, A, A);
  nor nor_2 (nor_2_out, B, B);
  nor nor_3 (nor_3_out, A, B);
  nor nor_4 (nor_4_out, A_2, B_2);
  nor nor_5 (nor_5_out, nor_1_out, nor_2_out);
  nor nor_6 (nor_6_out, A_2, nor_4_out);
  nor nor_7 (nor_7_out, nor_4_out, B_2);
  nor nor_8 (AB____A_B__prime, nor_5_out, nor_3_out);
  nor nor_9 (out_6, nor_6_out, nor_7_out);

  // Notes on the sheet:
  //   A'
  //   B'
  //   (A+B)'
  //   (A+B)'
  //   XOR using NOR
  //   AB
  //   XNOR using NOR
  //   (A + (A+B)')'
  //   (B + (A+B)')'
  //   (A + (A+B)')' + (B + (A+B)')'
endmodule
