// Logisim project lab 3.circ as structural Verilog: 5 circuits, main circuit main
module main (
  input  A,
  input  B,
  input  C,
  output out_4
);

  wire n3_input_and_gate_1_out_10, n3_input_and_gate_1_out_11, n3_input_and_gate_1_out_12,
       n7404_hex_inverter_not_1_out_10, n7404_hex_inverter_not_1_out_11, n7404_hex_inverter_not_1_out_12;

  _7404_Hex_inverter_NOT u_7404_hex_inverter_not_1 (
    .in_4(C), .in_5(A), .in_6(B), .out_10(n7404_hex_inverter_not_1_out_10),
    .out_11(n7404_hex_inverter_not_1_out_11), .out_12(n7404_hex_inverter_not_1_out_12));  // open: in_1, in_2, in_3, out_7, out_8, out_9
  _3_input_AND_gate u_3_input_and_gate_1 (
    .in_1(n7404_hex_inverter_not_1_out_10), .in_2(n7404_hex_inverter_not_1_out_11), .in_3(B), .in_4(A),
    .in_5(B), .in_6(n7404_hex_inverter_not_1_out_10), .in_7(C), .in_8(n7404_hex_inverter_not_1_out_12),
    .in_9(n7404_hex_inverter_not_1_out_11), .out_10(n3_input_and_gate_1_out_10),
    .out_11(n3_input_and_gate_1_out_11), .out_12(n3_input_and_gate_1_out_12));
  IC_4075_3_input_OR ic_4075_3_input_or_1 (
    .in_1(n3_input_and_gate_1_out_12), .in_2(n3_input_and_gate_1_out_10), .in_3(n3_input_and_gate_1_out_11),
    .out_10(out_4));  // open: in_4, in_5, in_6, in_7, in_8, in_9, out_11, out_12

  // Notes on the sheet:
  //   Canonical 1
endmodule

module _3_input_AND_gate (
  input  in_1,
  input  in_2,
  input  in_3,
  input  in_4,
  input  in_5,
  input  in_6,
  input  in_7,
  input  in_8,
  input  in_9,
  output out_10,
  output out_11,
  output out_12
);

  and and_1 (out_10, in_1, in_2, in_3);
  and and_2 (out_11, in_4, in_5, in_6);
  and and_3 (out_12, in_7, in_8, in_9);
endmodule

module IC_4075_3_input_OR (
  input  in_1,
  input  in_2,
  input  in_3,
  input  in_4,
  input  in_5,
  input  in_6,
  input  in_7,
  input  in_8,
  input  in_9,
  output out_10,
  output out_11,
  output out_12
);

  or or_1 (out_10, in_1, in_2, in_3);
  or or_2 (out_11, in_4, in_5, in_6);
  or or_3 (out_12, in_7, in_8, in_9);
endmodule

module _7404_Hex_inverter_NOT (
  input  in_1,
  input  in_2,
  input  in_3,
  input  in_4,
  input  in_5,
  input  in_6,
  output out_7,
  output out_8,
  output out_9,
  output out_10,
  output out_11,
  output out_12
);

  not not_1 (out_7, in_1);
  not not_2 (out_8, in_2);
  not not_3 (out_9, in_3);
  not not_4 (out_10, in_4);
  not not_5 (out_11, in_5);
  not not_6 (out_12, in_6);
endmodule

module _2nd_Conanical (
  input  A,
  input  B,
  input  C,
  output out_4
);

  wire ic_4075_3_input_or_1_out_10, ic_4075_3_input_or_1_out_11, ic_4075_3_input_or_1_out_12,
       ic_4075_3_input_or_2_out_11, ic_4075_3_input_or_2_out_12, n3_input_and_gate_1_out_12,
       n7404_hex_inverter_not_1_out_8, n7404_hex_inverter_not_1_out_9, n7404_hex_inverter_not_1_out_10,
       n7404_hex_inverter_not_1_out_11, n7404_hex_inverter_not_1_out_12;

  _7404_Hex_inverter_NOT u_7404_hex_inverter_not_1 (
    .in_2(B), .in_3(C), .in_4(B), .in_5(A), .in_6(C), .out_8(n7404_hex_inverter_not_1_out_8),
    .out_9(n7404_hex_inverter_not_1_out_9), .out_10(n7404_hex_inverter_not_1_out_10),
    .out_11(n7404_hex_inverter_not_1_out_11), .out_12(n7404_hex_inverter_not_1_out_12));  // open: in_1, out_7
  IC_4075_3_input_OR ic_4075_3_input_or_1 (
    .in_1(A), .in_2(B), .in_3(C), .in_4(n7404_hex_inverter_not_1_out_11), .in_5(B), .in_6(C),
    .in_7(n7404_hex_inverter_not_1_out_12), .in_8(n7404_hex_inverter_not_1_out_10), .in_9(B),
    .out_10(ic_4075_3_input_or_1_out_10), .out_11(ic_4075_3_input_or_1_out_11),
    .out_12(ic_4075_3_input_or_1_out_12));
  _3_input_AND_gate u_3_input_and_gate_1 (
    .in_4(ic_4075_3_input_or_2_out_12), .in_5(n3_input_and_gate_1_out_12),
    .in_6(ic_4075_3_input_or_2_out_11), .in_7(ic_4075_3_input_or_1_out_11),
    .in_8(ic_4075_3_input_or_1_out_12), .in_9(ic_4075_3_input_or_1_out_10), .out_11(out_4),
    .out_12(n3_input_and_gate_1_out_12));  // open: in_1, in_2, in_3, out_10
  IC_4075_3_input_OR ic_4075_3_input_or_2 (
    .in_4(n7404_hex_inverter_not_1_out_9), .in_5(n7404_hex_inverter_not_1_out_8),
    .in_6(n7404_hex_inverter_not_1_out_9), .in_7(n7404_hex_inverter_not_1_out_9), .in_8(B),
    .in_9(n7404_hex_inverter_not_1_out_11), .out_11(ic_4075_3_input_or_2_out_11),
    .out_12(ic_4075_3_input_or_2_out_12));  // open: in_1, in_2, in_3, out_10
endmodule
