// Logisim project Lab 4 performance.circ as structural Verilog: 4 circuits, main circuit Main circuit lab 4
module Main_circuit_lab_4 (
  input  W,
  input  X,
  input  Y,
  input  Z,
  output D,
  output B,
  output C,
  output A
);

  wire ic_7408_2_input_and_gate_1_out_9, ic_7408_2_input_and_gate_1_out_10,
       ic_7408_2_input_and_gate_1_out_11, ic_7408_2_input_and_gate_1_out_12,
       ic_7408_2_input_and_gate_2_out_9, ic_7408_2_input_and_gate_2_out_10,
       ic_7408_2_input_and_gate_2_out_11, ic_7408_2_input_and_gate_2_out_12, n7404_not_gate_1_out_10,
       n7404_not_gate_1_out_12, or_gate_icc_1_out_11, or_gate_icc_2_out_11;

  _7404_Not_gate u_7404_not_gate_1 (
    .in_4(Y), .in_5(Z), .in_6(X), .out_10(n7404_not_gate_1_out_10), .out_11(D),
    .out_12(n7404_not_gate_1_out_12));  // open: in_1, in_2, in_3, out_7, out_8, out_9
  IC_7408_2_input_And_gate ic_7408_2_input_and_gate_1 (
    .in_1(Y), .in_2(Z), .in_3(n7404_not_gate_1_out_10), .in_4(D), .in_5(Z), .in_6(X), .in_7(Y), .in_8(X),
    .out_9(ic_7408_2_input_and_gate_1_out_9), .out_10(ic_7408_2_input_and_gate_1_out_10),
    .out_11(ic_7408_2_input_and_gate_1_out_11), .out_12(ic_7408_2_input_and_gate_1_out_12));
  Or_gate_ICC or_gate_icc_1 (
    .in_1(ic_7408_2_input_and_gate_1_out_10), .in_2(ic_7408_2_input_and_gate_1_out_9), .in_5(W),
    .in_6(ic_7408_2_input_and_gate_1_out_11), .in_7(or_gate_icc_1_out_11),
    .in_8(ic_7408_2_input_and_gate_1_out_12), .out_9(C), .out_11(or_gate_icc_1_out_11), .out_12(A));  // open: in_3, in_4, out_10
  IC_7408_2_input_And_gate ic_7408_2_input_and_gate_2 (
    .in_1(ic_7408_2_input_and_gate_2_out_10), .in_2(D), .in_3(n7404_not_gate_1_out_10), .in_4(X), .in_5(Z),
    .in_6(n7404_not_gate_1_out_12), .in_7(n7404_not_gate_1_out_12), .in_8(Y),
    .out_9(ic_7408_2_input_and_gate_2_out_9), .out_10(ic_7408_2_input_and_gate_2_out_10),
    .out_11(ic_7408_2_input_and_gate_2_out_11), .out_12(ic_7408_2_input_and_gate_2_out_12));
  Or_gate_ICC or_gate_icc_2 (
    .in_5(ic_7408_2_input_and_gate_2_out_12), .in_6(ic_7408_2_input_and_gate_2_out_11),
    .in_7(ic_7408_2_input_and_gate_2_out_9), .in_8(or_gate_icc_2_out_11), .out_11(or_gate_icc_2_out_11),
    .out_12(B));  // open: in_1, in_2, in_3, in_4, out_9, out_10

  // Notes on the sheet:
  //   A = W+XZ+XY
  //   D=Z'
  //   C= Y'Z'+YZ
  //        B=X'Z+X'Y+XY'Z'
endmodule

module IC_7408_2_input_And_gate (
  input  in_1,
  input  in_2,
  input  in_3,
  input  in_4,
  input  in_5,
  input  in_6,
  input  in_7,
  input  in_8,
  output out_9,
  output out_10,
  output out_11,
  output out_12
);

  and and_1 (out_9, in_1, in_2);
  and and_2 (out_10, in_3, in_4);
  and and_3 (out_11, in_5, in_6);
  and and_4 (out_12, in_7, in_8);
endmodule

module Or_gate_ICC (
  input  in_1,
  input  in_2,
  input  in_3,
  input  in_4,
  input  in_5,
  input  in_6,
  input  in_7,
  input  in_8,
  output out_9,
  output out_10,
  output out_11,
  output out_12
);

  or or_1 (out_9, in_1, in_2);
  or or_2 (out_10, in_3, in_4);
  or or_3 (out_11, in_5, in_6);
  or or_4 (out_12, in_7, in_8);
endmodule

module _7404_Not_gate (
  input  in_1,
  input  in_2,
  input  in_3,
  input  in_4,
  input  in_5,
  input  in_6,
  output out_7,
  output out_8,
  output out_9,
  output out_10,
  output out_11,
  output out_12
);

  not not_1 (out_7, in_1);
  not not_2 (out_8, in_2);
  not not_3 (out_9, in_3);
  not not_4 (out_10, in_4);
  not not_5 (out_11, in_5);
  not not_6 (out_12, in_6);
endmodule
