// Logisim project Lab 5 CSE231.Task A.circ as structural Verilog: 3 circuits, main circuit XOR gate IC 7486
module main (
  input  in_1,
  input  in_2,
  input  in_3,
  input  in_4,
  input  in_5,
  input  in_6,
  input  in_7,
  input  in_8,
  input  in_9,
  output out_10,
  output [3:0] out_11
);

  wire xor_gate_ic_7486_1_out_9, xor_gate_ic_7486_1_out_10, xor_gate_ic_7486_1_out_11,
       xor_gate_ic_7486_1_out_12;

  XOR_gate_IC_7486 xor_gate_ic_7486_1 (
    .in_1(in_8), .in_2(in_9), .in_3(in_7), .in_4(in_9), .in_5(in_6), .in_6(in_9), .in_7(in_5), .in_8(in_9),
    .out_9(xor_gate_ic_7486_1_out_9), .out_10(xor_gate_ic_7486_1_out_10), .out_11(xor_gate_ic_7486_1_out_11),
    .out_12(xor_gate_ic_7486_1_out_12));
  IC_number_74283_adder ic_number_74283_adder_1 (
    .out_10(out_11), .out_11(out_10), .A1(in_4), .B1(xor_gate_ic_7486_1_out_10), .A2(in_3),
    .B2(xor_gate_ic_7486_1_out_9), .B3(xor_gate_ic_7486_1_out_11), .A4(in_1), .B4(xor_gate_ic_7486_1_out_12),
    .in_1(in_9), .A3(in_2));
endmodule

module XOR_gate_IC_7486 (
  input  in_1,
  input  in_2,
  input  in_3,
  input  in_4,
  input  in_5,
  input  in_6,
  input  in_7,
  input  in_8,
  output out_9,
  output out_10,
  output out_11,
  output out_12
);

  xor xor_1 (out_9, in_1, in_2);
  xor xor_2 (out_10, in_3, in_4);
  xor xor_3 (out_11, in_5, in_6);
  xor xor_4 (out_12, in_7, in_8);
endmodule

module IC_number_74283_adder (
  input  in_1,
  input  A1,
  input  B1,
  input  A2,
  input  B2,
  input  A3,
  input  B3,
  input  A4,
  input  B4,
  output [3:0] out_10,
  output out_11
);

  wire adder_1_cout, adder_2_cout, adder_3_cout;

  Adder #(.width(1)) adder_1 (.a(A1), .b(B1), .out(out_10[0]), .cin(in_1), .cout(adder_1_cout));
  Adder #(.width(1)) adder_2 (.a(A2), .b(B2), .out(out_10[1]), .cin(adder_1_cout), .cout(adder_2_cout));
  Adder #(.width(1)) adder_3 (.a(A3), .b(B3), .out(out_10[2]), .cin(adder_2_cout), .cout(adder_3_cout));
  Adder #(.width(1)) adder_4 (.a(A4), .b(B4), .out(out_10[3]), .cin(adder_3_cout), .cout(out_11));
endmodule
