// Logisim project lab 5 task 2.circ as structural Verilog: 4 circuits, main circuit main
module main (
  input  in_1,
  input  in_2,
  input  in_3,
  input  in_4,
  input  in_5,
  input  in_6,
  input  in_7,
  input  in_8,
  input  in_9,
  output out_10,
  output out_11,
  output out_12,
  output out_13,
  output out_14
);

  wire and_ic_1_out_10, and_ic_1_out_11, and_ic_1_out_12, ic_74283_arithmetic_adder_1_out_10,
       ic_74283_arithmetic_adder_1_out_11, ic_74283_arithmetic_adder_1_out_12,
       ic_74283_arithmetic_adder_1_out_13, ic_74283_arithmetic_adder_1_out_14, n7432_ic_or_gate_1_out_12;

  AND_Gate_IC and_ic_1 (
    .in_3(n7432_ic_or_gate_1_out_12), .in_4(ic_74283_arithmetic_adder_1_out_14),
    .in_5(ic_74283_arithmetic_adder_1_out_13), .in_6(ic_74283_arithmetic_adder_1_out_12),
    .in_7(ic_74283_arithmetic_adder_1_out_13), .in_8(ic_74283_arithmetic_adder_1_out_11),
    .out_10(and_ic_1_out_10), .out_11(and_ic_1_out_11), .out_12(and_ic_1_out_12));  // open: in_1, in_2, out_9
  _7432_IC_or_gate u_7432_ic_or_gate_1 (
    .in_7(and_ic_1_out_11), .in_8(and_ic_1_out_12), .out_12(n7432_ic_or_gate_1_out_12));  // open: in_1, in_2, in_3, in_4, in_5, in_6, out_9, out_10, out_11
  IC_74283_Arithmetic_adder ic_74283_arithmetic_adder_1 (
    .in_2(in_4), .in_3(in_8), .in_4(in_3), .in_5(in_7), .in_6(in_2), .in_7(in_6), .in_8(in_1), .in_9(in_5),
    .out_10(ic_74283_arithmetic_adder_1_out_10), .out_11(ic_74283_arithmetic_adder_1_out_11),
    .out_12(ic_74283_arithmetic_adder_1_out_12), .out_13(ic_74283_arithmetic_adder_1_out_13),
    .out_14(ic_74283_arithmetic_adder_1_out_14));  // open: in_1
  IC_74283_Arithmetic_adder ic_74283_arithmetic_adder_2 (
    .in_2(in_9), .in_3(ic_74283_arithmetic_adder_1_out_10), .in_4(and_ic_1_out_10),
    .in_5(ic_74283_arithmetic_adder_1_out_11), .in_6(and_ic_1_out_10),
    .in_7(ic_74283_arithmetic_adder_1_out_12), .in_8(in_9), .in_9(ic_74283_arithmetic_adder_1_out_13),
    .out_10(out_14), .out_11(out_13), .out_12(out_12), .out_13(out_11), .out_14(out_10));  // open: in_1
endmodule

module IC_74283_Arithmetic_adder (
  input  in_1,
  input  in_2,
  input  in_3,
  input  in_4,
  input  in_5,
  input  in_6,
  input  in_7,
  input  in_8,
  input  in_9,
  output out_10,
  output out_11,
  output out_12,
  output out_13,
  output out_14
);

  wire adder_1_cout, adder_2_cout, adder_3_cout;

  Adder #(.width(1)) adder_1 (.a(in_2), .b(in_3), .out(out_10), .cin(in_1), .cout(adder_1_cout));
  Adder #(.width(1)) adder_2 (.a(in_4), .b(in_5), .out(out_11), .cin(adder_1_cout), .cout(adder_2_cout));
  Adder #(.width(1)) adder_3 (.a(in_6), .b(in_7), .out(out_12), .cin(adder_2_cout), .cout(adder_3_cout));
  Adder #(.width(1)) adder_4 (.a(in_8), .b(in_9), .out(out_13), .cin(adder_3_cout), .cout(out_14));
endmodule

module _7432_IC_or_gate (
  input  in_1,
  input  in_2,
  input  in_3,
  input  in_4,
  input  in_5,
  input  in_6,
  input  in_7,
  input  in_8,
  output out_9,
  output out_10,
  output out_11,
  output out_12
);

  or or_1 (out_9, in_1, in_2);
  or or_2 (out_10, in_3, in_4);
  or or_3 (out_11, in_5, in_6);
  or or_4 (out_12, in_7, in_8);
endmodule

module AND_Gate_IC (
  input  in_1,
  input  in_2,
  input  in_3,
  input  in_4,
  input  in_5,
  input  in_6,
  input  in_7,
  input  in_8,
  output out_9,
  output out_10,
  output out_11,
  output out_12
);

  and and_1 (out_9, in_1, in_2);
  and and_2 (out_10, in_3, in_4);
  and and_3 (out_11, in_5, in_6);
  and and_4 (out_12, in_7, in_8);
endmodule
