// Logisim project lab 7 task b.circ as structural Verilog: 5 circuits, main circuit main
module main (
  input  A,
  input  B,
  input  C,
  input  D
);

  wire a_out, and_1_out, and_2_out, and_3_out, and_4_out, and_5_out, B_prime_D_prime_out, BD_out,
       BD_prime_out, CD_out, CD_prime_out, not_1_out, not_2_out, not_3_out, not_4_out, or_1_out, or_2_out,
       or_3_out, or_4_out, or_5_out, or_6_out;

  not not_1 (not_1_out, A);
  not not_2 (not_2_out, B);
  not not_3 (not_3_out, C);
  not not_4 (not_4_out, D);
  and and_1 (and_1_out, B, and_5_out);
  and CD_prime (CD_prime_out, C, not_4_out);
  and BD (BD_out, B, D);
  and CD (CD_out, D, C);
  and and_2 (and_2_out, not_3_out, not_4_out);
  and B_prime_D_prime (B_prime_D_prime_out, not_2_out, not_4_out);
  and and_3 (and_3_out, not_2_out, C);
  and and_4 (and_4_out, B, not_3_out);
  and BD_prime (BD_prime_out, B, not_4_out);
  and and_5 (and_5_out, D, not_3_out);
  or u_a (a_out, A, BD_out, B_prime_D_prime_out, C);
  or or_1 (or_1_out, CD_out, and_2_out, not_2_out);
  or or_2 (or_2_out, B, not_3_out, D);
  or or_3 (or_3_out, A, CD_prime_out, B_prime_D_prime_out, and_3_out, and_1_out);
  or or_4 (or_4_out, CD_prime_out, B_prime_D_prime_out);
  or or_5 (or_5_out, A, and_4_out, BD_prime_out, and_2_out);
  or or_6 (or_6_out, A, and_3_out, and_4_out, BD_prime_out);
  _7_Segment_Display u_7_segment_display_1 (
    .g(or_6_out), .f(or_5_out), .a(a_out), .b(or_1_out), .e(or_4_out), .d(or_3_out), .c(or_2_out));  // open: dp

  // Notes on the sheet:
  //   BC'D
  //   C'D'
  //   B'C
  //   BC'
  //   C'D
  //   d
  //   A+C+BD+B'D'
  //   CD+C'D'+B'
  //   b
  //   B+C'+D
  //   c
  //   CD'+B'D'
  //   e
  //   A+BC'+BD'+C'D'
  //   f
  //   A+B'C+BC'+BD'
  //   g
  //   A+CD'+B'D'+B'C+BC'D
endmodule

module \and  (
  input  in_1,
  input  in_2,
  input  in_3,
  input  in_4,
  input  in_5,
  input  in_6,
  input  in_7,
  input  in_8,
  output out_9,
  output out_10,
  output out_11,
  output out_12
);

  and and_1 (out_9, in_1, in_2);
  and and_2 (out_10, in_3, in_4);
  and and_3 (out_11, in_5, in_6);
  and and_4 (out_12, in_7, in_8);
endmodule

module \or  (
  input  in_1,
  input  in_2,
  input  in_3,
  input  in_4,
  input  in_5,
  input  in_6,
  input  in_7,
  input  in_8,
  input  in_9,
  output out_10,
  output out_11,
  output out_12
);

  or or_1 (out_10, in_1, in_2, in_3);
  or or_2 (out_11, in_4, in_5, in_6);
  or or_3 (out_12, in_7, in_8, in_9);
endmodule

module \not  (
  input  in_1,
  input  in_2,
  input  in_3,
  input  in_4,
  input  in_5,
  input  in_6,
  output out_7,
  output out_8,
  output out_9,
  output out_10,
  output out_11,
  output out_12
);

  not not_1 (out_7, in_1);
  not not_2 (out_8, in_2);
  not not_3 (out_9, in_3);
  not not_4 (out_10, in_4);
  not not_5 (out_11, in_5);
  not not_6 (out_12, in_6);
endmodule

module or_2 (
  input  in_1,
  input  in_2,
  input  in_3,
  input  in_4,
  input  in_5,
  input  in_6,
  input  in_7,
  input  in_8,
  output out_9,
  output out_10,
  output out_11,
  output out_12
);

  or or_1 (out_9, in_1, in_2);
  or or_2 (out_10, in_3, in_4);
  or or_3 (out_11, in_5, in_6);
  or or_4 (out_12, in_7, in_8);
endmodule
