// Logisim project week 7.circ as structural Verilog: 1 circuit, main circuit main
module main (
  input  D,
  input  [2:0] ABC,
  output out_3
);

  Multiplexer #(.select(3), .enable("false")) multiplexer_1 (
    .in0(1'b1), .in1(D), .in2(D), .in3(1'b0), .in4(1'b1), .in5(1'b0), .in6(1'b0), .in7(1'b1), .out(out_3),
    .sel(ABC));
endmodule
