// Logisim project c.circ as structural Verilog: 1 circuit, main circuit main
module main (
  input  [2:0] C__B__A,
  output Y0,
  output Y1,
  output Y2,
  output Y3,
  output Y4,
  output Y5,
  output Y6,
  output Y7
);

  wire decoder_1_out0, decoder_1_out1, decoder_1_out2, decoder_1_out3, decoder_1_out4, decoder_1_out5,
       decoder_1_out6, decoder_1_out7;

  Decoder #(.select(3), .enable("false")) decoder_1 (
    .out0(decoder_1_out0), .out1(decoder_1_out1), .out2(decoder_1_out2), .out3(decoder_1_out3),
    .out4(decoder_1_out4), .out5(decoder_1_out5), .out6(decoder_1_out6), .out7(decoder_1_out7), .sel(C__B__A));
  not not_1 (Y4, decoder_1_out4);
  not not_2 (Y5, decoder_1_out5);
  not not_3 (Y6, decoder_1_out6);
  not not_4 (Y7, decoder_1_out7);
  not not_5 (Y3, decoder_1_out3);
  not not_6 (Y2, decoder_1_out2);
  not not_7 (Y0, decoder_1_out0);
  not not_8 (Y1, decoder_1_out1);
endmodule
