// Logisim project D flip flop.circ as structural Verilog: 1 circuit, main circuit main
module main (
  input  A,
  input  B,
  input  X
);

  wire and_1_out, and_2_out, and_3_out, clock_1_out, not_1_out, not_2_out, not_3_out, or_1_out;

  not not_1 (not_1_out, A);
  not not_2 (not_2_out, B);
  not not_3 (not_3_out, X);
  and and_1 (and_1_out, not_1_out, not_2_out, X);
  and and_2 (and_2_out, A, B, X);
  and and_3 (and_3_out, not_1_out, not_3_out, B);
  or or_1 (or_1_out, and_1_out, and_2_out, and_3_out);
  Clock clock_1 (.out(clock_1_out));
  D_Flip_Flop d_ff_1 (.clk(clock_1_out), .D(or_1_out));  // open: Q, Qn, preset, en, reset
  D_Flip_Flop d_ff_2 (.clk(clock_1_out), .D(not_2_out));  // open: Q, Qn, preset, en, reset

  // Notes on the sheet:
  //   B'
  //              DA= A'B'X+ ABX+A'BX'
endmodule
